// Digital circuit hw1_4bit_ripple_carry_adder.dig as structural Verilog
module hw1_4bit_ripple_carry_adder (
  input  A_0,
  input  B_0,
  input  C_in,
  input  A_1,
  input  B_1,
  input  A_2,
  input  B_2,
  input  A_3,
  input  B_3,
  output S_0,
  output S_1,
  output S_2,
  output S_3,
  output C_out
);

  wire and_1_out, and_2_out, and_3_out, and_4_out, and_5_out, and_6_out, and_7_out, and_8_out, or_1_out,
       or_2_out, or_4_out, xor_1_out, xor_2_out, xor_3_out, xor_4_out;

  xor xor_1 (xor_1_out, B_0, A_0);
  xor xor_2 (xor_2_out, B_1, A_1);
  xor xor_3 (xor_3_out, B_2, A_2);
  xor xor_4 (xor_4_out, B_3, A_3);
  xor xor_5 (S_2, xor_3_out, or_1_out);
  and and_1 (and_1_out, B_2, A_2);
  and and_2 (and_2_out, or_1_out, xor_3_out);
  xor xor_6 (S_3, xor_4_out, or_2_out);
  and and_3 (and_3_out, B_3, A_3);
  and and_4 (and_4_out, or_2_out, xor_4_out);
  xor xor_7 (S_0, xor_1_out, C_in);
  and and_5 (and_5_out, B_0, A_0);
  and and_6 (and_6_out, C_in, xor_1_out);
  xor xor_8 (S_1, xor_2_out, or_4_out);
  and and_7 (and_7_out, B_1, A_1);
  and and_8 (and_8_out, or_4_out, xor_2_out);
  or or_1 (or_1_out, and_7_out, and_8_out);
  or or_2 (or_2_out, and_1_out, and_2_out);
  or or_3 (C_out, and_3_out, and_4_out);
  or or_4 (or_4_out, and_5_out, and_6_out);
endmodule
