// Digital circuit hw1_multiplier.dig as structural Verilog
module hw1_multiplier (
  input  A_0,
  input  A_1,
  input  B_0,
  input  B_1,
  output P_0,
  output P_1,
  output P_2,
  output P_3
);

  wire and_2_out, and_3_out, and_4_out, and_5_out;

  and and_1 (P_0, A_0, B_0);
  and and_2 (and_2_out, A_1, B_0);
  and and_3 (and_3_out, A_0, B_1);
  and and_4 (and_4_out, A_1, B_1);
  xor xor_1 (P_1, and_2_out, and_3_out);
  and and_5 (and_5_out, and_2_out, and_3_out);
  xor xor_2 (P_2, and_5_out, and_4_out);
  and and_6 (P_3, and_5_out, and_4_out);

  // Notes on the sheet:
  //   Half-Adder
endmodule
